# Fritzing sketch 00.LEDbarKristianMedri (saved by Fritzing 0.9.4)
circuit board: 5.70353cm x 4.5cm
breadboards: 1

parts:
  J1 = STM32F103C8T6 blue mini board
  00_LEDbarKristian = LED_BARGRAPH_10 [package=led_bargaph_10]
  J3 = female pin header, 2 pins [form="♀ (female)"]
  R12 = Resistor [tolerance=±5% resistance=220 package="0603 [SMD]"]
  R13 = Resistor [tolerance=±5% resistance=220 package="0603 [SMD]"]
  R14 = Resistor [tolerance=±5% resistance=220 package="0603 [SMD]"]
  R15 = Resistor [tolerance=±5% resistance=220 package="0603 [SMD]"]
  R16 = Resistor [tolerance=±5% resistance=220 package="0603 [SMD]"]
  R17 = Resistor [tolerance=±5% resistance=220 package="0603 [SMD]"]
  R18 = Resistor [tolerance=±5% resistance=220 package="0603 [SMD]"]
  R19 = Resistor [tolerance=±5% resistance=220 package="0603 [SMD]"]
  R20 = Resistor [tolerance=±5% resistance=220 package="0603 [SMD]"]
  R21 = Resistor [tolerance=±5% resistance=220 package="0603 [SMD]"]
  S1 = JOYSTICK_MINI [package=joystick_mini]
  B5 = male pin header, 3 pins [form="♂ (male)"]
  B6 = male pin header, 2 pins [form="♂ (male)"]
  B7 = male pin header, 2 pins [form="♂ (male)"]
  B4 = male pin header, 2 pins [form="♂ (male)"]
  B2 = male pin header, 6 pins [form="♂ (male)"]
  U2 = BME280r2 [package=lga8]  # not connected
  U3 = PCF8574 [package="DIP16 [THT]"]  # not connected
  U4 = Thumb Joystick [package=joystick]  # not connected
  7_Segment1 = 7 Segment Display  # not connected

nets:
  N1: J1.A8, B5.pin1
  N2: J1.A9, B2.pin2
  N3: J1.A10, B2.pin3
  N4: J1.B5, S1.CENT
  N5: J1.B6, S1.UP
  N6: J1.B7, S1.DOWN
  N7: J1.5V, B5.pin2
  GND: J1.G, J1.GND, S1.GND, B5.pin3, B2.pin6
  N8: J1.3.3V, B4.pin1
  N9: J1.A0, 00_LEDbarKristian.A_C
  N10: J1.A1, 00_LEDbarKristian.B_C
  N11: J1.A2, 00_LEDbarKristian.C_C
  N12: J1.A3, 00_LEDbarKristian.D_C
  N13: J1.A4, 00_LEDbarKristian.E_C
  N14: J1.A5, 00_LEDbarKristian.F_C
  N15: J1.A6, 00_LEDbarKristian.G_C
  N16: J1.A7, 00_LEDbarKristian.H_C
  N17: J1.B0, B7.pin1
  N18: J1.B1, B6.pin1
  N19: 00_LEDbarKristian.A_A, R12.Pin_0
  N20: 00_LEDbarKristian.B_A, R13.Pin_0
  N21: 00_LEDbarKristian.C_A, R14.Pin_0
  N22: 00_LEDbarKristian.D_A, R15.Pin_0
  N23: 00_LEDbarKristian.E_A, R16.Pin_0
  N24: 00_LEDbarKristian.F_A, R17.Pin_0
  N25: 00_LEDbarKristian.G_A, R18.Pin_0
  N26: 00_LEDbarKristian.H_A, R19.Pin_0
  N27: 00_LEDbarKristian.I_A, R20.Pin_0
  N28: 00_LEDbarKristian.J_A, R21.Pin_0
  N29: 00_LEDbarKristian.J_C, J3.pin1
  N30: 00_LEDbarKristian.I_C, J3.pin2
  N31: R12.Pin_1, R13.Pin_1, R14.Pin_1, R15.Pin_1, R16.Pin_1, R17.Pin_1, R18.Pin_1, R19.Pin_1, R20.Pin_1, R21.Pin_1, B4.pin2
  N32: S1.RIGHT, B7.pin2
  N33: S1.LEFT, B6.pin2

notes:
  PA0
  G
  G G3.3
  VBAT
  3.3
  RX
  TX
  5V G
