# Fritzing sketch CBA_2020_10_01 (saved by Fritzing 0.9.4)
circuit board: 10cm x 10cm
breadboards: 1

parts:
  J1 = STM32F103C8T6 blue mini board
  J11 = female pin header, 2 pins [form="♀ (female)"]
  R12 = Resistor [tolerance=±5% resistance=220 package="0603 [SMD]"]
  R13 = Resistor [tolerance=±5% resistance=220 package="0603 [SMD]"]
  R14 = Resistor [tolerance=±5% resistance=220 package="0603 [SMD]"]
  R15 = Resistor [tolerance=±5% resistance=220 package="0603 [SMD]"]
  R16 = Resistor [tolerance=±5% resistance=220 package="0603 [SMD]"]
  R17 = Resistor [tolerance=±5% resistance=220 package="0603 [SMD]"]
  R18 = Resistor [tolerance=±5% resistance=220 package="0603 [SMD]"]
  R19 = Resistor [tolerance=±5% resistance=220 package="0603 [SMD]"]
  R20 = Resistor [tolerance=±5% resistance=1k package="0603 [SMD]"]
  R21 = Resistor [tolerance=±5% resistance=1k package="0603 [SMD]"]
  J5 = male pin header, 3 pins [form="♂ (male)"]  # not connected
  J6 = male pin header, 2 pins [form="♂ (male)"]
  J7 = male pin header, 2 pins [form="♂ (male)"]
  J4 = male pin header, 2 pins [form="♂ (male)"]
  J10 = male pin header, 6 pins [form="♂ (male)"]
  BME280 = BME280r2 [package=lga8]
  PCF8574 = PCF8574 [package="DIP16 [THT]"]
  Joystick = Thumb Joystick [package=joystick]
  U5 = MCP73831 [package=sot23-5]
  JP1 = Header 2 [package=jst-2-pth-kit]
  R22 = Resistor [tolerance=±5% resistance=10k package="0603 [SMD]"]
  DONE = smd LED [color="Green (560nm)" package="0603 [SMD]"]
  CHG = smd LED [color="Red (633nm)" package="0603 [SMD]"]
  D2 = DIODE-SCHOTTKY [package=sma-diode]
  74VHC125MTC = TSSOP14 [chip_label=IC package=TSSOP]  # not connected
  OLED = 27 pin OLED
  LM75 = MSOP8 [chip_label=IC package=MSOP8]  # not connected
  Buzzer = Buzzer 12mm [package=buzzer-cmt1102]  # not connected
  Flash = SPI_FLASH-X25XX [package=so08]
  7_SegmentG1 = 7 Segment DisplayG
  SDA = male pin header, 3 pins [form="♂ (male)"]
  SCL = male pin header, 3 pins [form="♂ (male)"]
  U8 = microSD Socket [package=micro-sd-socket-pp]  # not connected
  J3 = STM32F103C8T6 blue mini board
  SDAslave = male pin header, 3 pins [form="♂ (male)"]
  SCLslave = male pin header, 3 pins [form="♂ (male)"]
  J12 = Basic Servo  # not connected
  DS1 = DS18B20 1-Wire Temperature Sensor [part_number=DS18B20]
  SCK = male pin header, 3 pins [form="♂ (male)"]
  MISO = male pin header, 3 pins [form="♂ (male)"]  # not connected
  MOSI = male pin header, 3 pins [form="♂ (male)"]  # not connected
  NSS = male pin header, 3 pins [form="♂ (male)"]
  C6 = Tantalum Capacitor [capacitance=10µF package="C 6032 [SMD, tantalum]"]
  C7 = Tantalum Capacitor [capacitance=10µF package="C 6032 [SMD, tantalum]"]
  R23 = Resistor [tolerance=±5% resistance=4.7k package="0603 [SMD]"]
  C8 = Ceramic Capacitor [capacitance=100nF package="0603 [SMD, multilayer]"]  # not connected
  J8 = male pin header, 8 pins [form="♂ (male)"]  # not connected
  J9 = male pin header, 8 pins [form="♂ (male)"]  # not connected
  R24 = Resistor [tolerance=±5% resistance=4.7k package="0603 [SMD]"]

nets:
  N1: J1.B12, DS1.DQ, R24.Pin_0
  N2: J1.A9, J10.pin2
  N3: J1.A10, J10.pin3
  N4: J1.A15, NSS.pin1
  N5: J1.B3, SCK.pin1
  N6: J1.B6, SCL.pin1, SCLslave.pin1
  N7: J1.B7, SDA.pin1, SDAslave.pin1
  N8: J1.B8, SCL.pin3
  N9: J1.B9, SDA.pin3
  5V: J1.5V, U5.VIN, CHG.anode, D2.C, C6.+
  GND/Gnd/VSS: J1.G, J1.GND, J10.pin6, BME280.GND, PCF8574.A0, PCF8574.A1, PCF8574.A2, PCF8574.GND, Joystick.SEL-, Joystick.H-, Joystick.V-, U5.VSS, JP1.1, R22.Pin_0, DONE.cathode, OLED.pin9, OLED.pin10, OLED.pin21, OLED.pin22, OLED.pin23, OLED.pin24, OLED.pin25, Flash.GND, 7_SegmentG1.common_cathode, J3.G, J3.GND, DS1.GND, C6.-, C7.-
  3.3V/VCC: J1.3.3V, J11.pin2, J4.pin1, OLED.pin17, DS1.VDD, R23.Pin_1, R24.Pin_1
  N10: J1.C14, PCF8574.INT
  N11: J1.A0, Joystick.H
  N12: J1.A2, Joystick.V
  N13: J1.A3, R19.Pin_1
  N14: J1.B0, J7.pin1
  N15: J1.B1, J6.pin1
  N16: R12.Pin_0, 7_SegmentG1.Segment_A
  N17: R12.Pin_1, PCF8574.P0
  N18: R13.Pin_0, 7_SegmentG1.Segment_B
  N19: R13.Pin_1, PCF8574.P1
  N20: R14.Pin_0, 7_SegmentG1.Segment_C
  N21: R14.Pin_1, PCF8574.P2
  N22: R15.Pin_0, PCF8574.P3
  N23: R15.Pin_1, 7_SegmentG1.Segment_D
  N24: R16.Pin_0, PCF8574.P4
  N25: R16.Pin_1, 7_SegmentG1.Segment_E
  N26: R17.Pin_0, PCF8574.P5
  N27: R17.Pin_1, 7_SegmentG1.Segment_F
  N28: R18.Pin_0, PCF8574.P6
  N29: R18.Pin_1, 7_SegmentG1.Segment_G
  N30: R19.Pin_0, 7_SegmentG1.Segment_DP
  N31: R20.Pin_0, CHG.cathode
  N32: R20.Pin_1, R21.Pin_1, U5.STAT
  N33: R21.Pin_0, DONE.anode
  N34: J4.pin2, PCF8574.VCC, Joystick.V+, Joystick.H+
  N35: PCF8574.P7, Joystick.SEL+
  N36: PCF8574.SCL, SCL.pin2
  N37: PCF8574.SDA, SDA.pin2
  N38: U5.VBAT, JP1.2, D2.A, C7.+
  N39: U5.PROG, R22.Pin_1
  VDD: OLED.pin8
  CS: OLED.pin11, NSS.pin2, R23.Pin_0
  RES: OLED.pin12
  DC: OLED.pin13
  SCLK: OLED.pin18
  SDIN: OLED.pin19
  N40: J3.B6, SCLslave.pin2
  N41: J3.B7, SDAslave.pin2
  SCK: SCK.pin2

notes:
  PA0
  G
  G G3.3
  VBAT
  3.3
  RX
  TX
  5V G
  CBA_2020_10_01
  J0

custom parts:
  7 Segment DisplayG: 7 Segment Display with common cathode.(fixed G)
