# Fritzing sketch CBA_2020_10_11 (saved by Fritzing 0.9.4)
circuit board: 10cm x 10cm
circuit board: 10cm x 10cm
breadboards: 1

parts:
  J1 = STM32F103C8T6 blue mini board
  J11 = female pin header, 2 pins [form="♀ (female)"]
  R12 = Resistor [tolerance=±5% resistance=220 package="0603 [SMD]"]
  R13 = Resistor [tolerance=±5% resistance=220 package="0603 [SMD]"]
  R14 = Resistor [tolerance=±5% resistance=220 package="0603 [SMD]"]
  R15 = Resistor [tolerance=±5% resistance=220 package="0603 [SMD]"]
  R16 = Resistor [tolerance=±5% resistance=220 package="0603 [SMD]"]
  R17 = Resistor [tolerance=±5% resistance=220 package="0603 [SMD]"]
  R18 = Resistor [tolerance=±5% resistance=220 package="0603 [SMD]"]
  R19 = Resistor [tolerance=±5% resistance=220 package="0603 [SMD]"]
  R20 = Resistor [tolerance=±5% resistance=1k package="0603 [SMD]"]
  R21 = Resistor [tolerance=±5% resistance=1k package="0603 [SMD]"]
  J6 = male pin header, 2 pins [form="♂ (male)"]
  J7 = male pin header, 2 pins [form="♂ (male)"]
  J4 = male pin header, 2 pins [form="♂ (male)"]
  J10 = male pin header, 6 pins [form="♂ (male)"]
  BME280 = BME280r2 [package=lga8]
  PCF8574 = PCF8574 [package="DIP16 [THT]"]
  Joystick = Thumb Joystick [package=joystick]
  U5 = MCP73831 [package=sot23-5]
  JP1 = Header 2 [package=jst-2-pth-kit]
  R22 = Resistor [tolerance=±5% resistance=10k package="0603 [SMD]"]
  DONE = smd LED [color="Green (560nm)" package="0603 [SMD]"]
  CHG = smd LED [color="Red (633nm)" package="0603 [SMD]"]
  D2 = DIODE-SCHOTTKY [package=sma-diode]
  74VHC125MTC = TSSOP14 [chip_label=IC package=TSSOP]
  LM75 = MSOP8 [chip_label=IC package=MSOP8]
  Buzzer = Buzzer 12mm [package=buzzer-cmt1102]
  Flash = SPI_FLASH-X25XX [package=so08]
  7_Segment = 7 Segment DisplayG
  J26 = male pin header, 3 pins [form="♂ (male)"]
  J27 = male pin header, 3 pins [form="♂ (male)"]
  J3 = STM32F103C8T6 blue mini board
  DS1 = DS18B20 1-Wire Temperature Sensor [part_number=DS18B20]
  R24 = Resistor [tolerance=±5% resistance=4.7k package="0603 [SMD]"]
  R25 = Resistor [tolerance=±5% resistance=4.7k package="0603 [SMD]"]
  R26 = Resistor [tolerance=±5% resistance=4.7k package="0603 [SMD]"]
  J12 = male pin header, 2 pins [form="♂ (male)"]
  J14 = male pin header, 3 pins [form="♂ (male)"]
  J15 = male pin header, 3 pins [form="♂ (male)"]
  J23 = male pin header, 3 pins [form="♂ (male)"]
  J22 = male pin header, 3 pins [form="♂ (male)"]
  J21 = male pin header, 3 pins [form="♂ (male)"]
  J20 = male pin header, 3 pins [form="♂ (male)"]
  J19 = male pin header, 3 pins [form="♂ (male)"]
  J18 = male pin header, 3 pins [form="♂ (male)"]
  J17 = male pin header, 3 pins [form="♂ (male)"]
  J16 = male pin header, 3 pins [form="♂ (male)"]
  J13 = male pin header, 3 pins [form="♂ (male)"]
  J24 = male pin header, 3 pins [form="♂ (male)"]
  Q1 = npn-Powertransistor [package="TO220 [THT]"]
  R27 = Resistor [tolerance=±5% resistance=1.0k package="0603 [SMD]"]
  R29 = Resistor [tolerance=±5% resistance=4.7k package="0603 [SMD]"]
  R30 = Resistor [tolerance=±5% resistance=4.7k package="0603 [SMD]"]
  J25 = male pin header, 2 pins [form="♂ (male)"]
  J35 = male pin header, 2 pins [form="♂ (male)"]
  R31 = Resistor [tolerance=±5% resistance=390k package="0603 [SMD]"]
  C23 = Ceramic Capacitor [capacitance=0.1µF voltage=16V package="0603 [SMD, multilayer]"]
  C22 = Ceramic Capacitor [capacitance=2.2µF package="0603 [SMD, multilayer]"]
  C21 = Ceramic Capacitor [capacitance=2.2µF package="0603 [SMD, multilayer]"]
  OLED = 30 pin OLED
  R32 = Resistor [tolerance=±5% resistance=4.7k package="0603 [SMD]"]  # not connected
  J42 = male pin header, 2 pins [form="♂ (male)"]
  J41 = male pin header, 2 pins [form="♂ (male)"]
  J44 = male pin header, 2 pins [form="♂ (male)"]
  R23 = Resistor [tolerance=±5% resistance=4.7k package="0603 [SMD]"]
  U9 = microSD Socket
  C9 = Ceramic Capacitor [capacitance=100nF package="0603 [SMD, multilayer]"]
  C8 = Ceramic Capacitor [capacitance=100nF package="0603 [SMD, multilayer]"]
  R33 = Resistor [tolerance=±5% resistance=10 package="0603 [SMD]"]
  J5 = Basic Servo
  R28 = Resistor [tolerance=±5% resistance=4.7k package="0603 [SMD]"]
  J43 = male pin header, 2 pins [form="♂ (male)"]
  J40 = male pin header, 3 pins [form="♂ (male)"]
  J39 = male pin header, 3 pins [form="♂ (male)"]
  J38 = male pin header, 2 pins [form="♂ (male)"]
  J37 = male pin header, 2 pins [form="♂ (male)"]
  J8 = male pin header, 2 pins [form="♂ (male)"]
  J9 = male pin header, 2 pins [form="♂ (male)"]
  J36 = male pin header, 2 pins [form="♂ (male)"]
  J28 = male pin header, 2 pins [form="♂ (male)"]
  J29 = male pin header, 2 pins [form="♂ (male)"]
  J30 = male pin header, 2 pins [form="♂ (male)"]
  R34 = Resistor [tolerance=±5% resistance=220 package="0603 [SMD]"]
  R35 = Resistor [tolerance=±5% resistance=220 package="0603 [SMD]"]
  R36 = Resistor [tolerance=±5% resistance=220 package="0603 [SMD]"]
  Right = smd LED [color="Green (560nm)" package="0603 [SMD]"]
  Left = smd LED [color="Green (560nm)" package="0603 [SMD]"]
  Brake = smd LED [color="Red (633nm)" package="0603 [SMD]"]
  J31 = male pin header, 2 pins [form="♂ (male)"]
  J32 = male pin header, 4 pins [form="♂ (male)"]
  R37 = Resistor [tolerance=±5% resistance=220 package="0603 [SMD]"]
  J33 = male pin header, 2 pins [form="♂ (male)"]
  J34 = male pin header, 2 pins [form="♂ (male)"]
  R38 = Resistor [tolerance=±5% resistance=10k package="0603 [SMD]"]
  C7 = Tantalum Capacitor [capacitance=10µF package="A 3216 [SMD, tantalum]"]
  C6 = Tantalum Capacitor [capacitance=10µF package="A 3216 [SMD, tantalum]"]
  C25 = Tantalum Capacitor [capacitance=10µF package="A 3216 [SMD, tantalum]"]
  C26 = Tantalum Capacitor [capacitance=10µF package="A 3216 [SMD, tantalum]"]
  C24 = Tantalum Capacitor [capacitance=10µF package="A 3216 [SMD, tantalum]"]

nets (from the pcb view):
  N1: J1.B12, J20.pin3, J16.pin3, J24.pin3, J35.pin1
  N2: J1.B13, J15.pin3, J23.pin3, J19.pin3
  N3: J1.B14, J14.pin3, J22.pin3, J18.pin3
  N4: J1.B15, J21.pin3, J17.pin3, J13.pin3
  N5: J1.A8, Q1.base
  N6: J1.A9, J10.pin2
  N7: J1.A10, J10.pin3
  N8: J1.A11, J8.pin1
  N9: J1.A12, J9.pin1
  N10: J1.A15, J43.pin1
  N11: J1.B3, J42.pin1
  N12: J1.B5, J41.pin1
  N13: J1.B6, J27.pin1
  N14: J1.B7, J26.pin1, J37.pin1
  N15: J1.B8, J27.pin3, J38.pin1, J28.pin1
  N16: J1.B9, J26.pin3, J29.pin1
  5V: J1.5V, U5.VIN, CHG.anode, D2.C, 74VHC125MTC.14, R27.Pin_1, R33.Pin_1, C6.+
  GND: J1.G, J1.GND, J10.pin6, BME280.GND, PCF8574.A0, PCF8574.A1, PCF8574.A2, PCF8574.GND, Joystick.SEL-, Joystick.H-, Joystick.V-, U5.VSS, JP1.1, R22.Pin_0, DONE.cathode, 74VHC125MTC.1, 74VHC125MTC.4, 74VHC125MTC.5, 74VHC125MTC.7, 74VHC125MTC.9, 74VHC125MTC.10, 74VHC125MTC.12, 74VHC125MTC.13, LM75.4, LM75.5, LM75.6, LM75.7, Flash.GND, 7_Segment.common_cathode, J3.G, DS1.GND, R25.Pin_0, Q1.emitter, R31.Pin_0, C23.0, OLED.pin1, OLED.pin8, OLED.pin10, OLED.pin11, OLED.pin12, OLED.pin16, OLED.pin17, OLED.pin21, OLED.pin22, OLED.pin23, OLED.pin24, OLED.pin25, OLED.pin29, OLED.pin30, U9.GND, C9.0, C8.0, J5.gnd, J32.pin4, C7.-, C6.-, C25.-, C26.-, C24.-
  3.3V: J1.3.3V, J11.pin2, J6.pin2, J7.pin2, J4.pin1, Joystick.V+, Joystick.H+, LM75.8, DS1.VDD, R24.Pin_1, R29.Pin_1, J44.pin1, U9.VCC, R28.Pin_1, J36.pin2
  N17: J1.C14, J25.pin1
  N18: J1.A0, Joystick.H
  N19: J1.A1, 74VHC125MTC.2
  N20: J1.A2, Joystick.V
  N21: J1.A3, R19.Pin_1
  N22: J1.A4, J20.pin1, J16.pin1, J24.pin1
  N23: J1.A5, J15.pin1, J23.pin1, J19.pin1
  N24: J1.A6, J14.pin1, J22.pin1, J18.pin1
  N25: J1.A7, J21.pin1, J17.pin1, J13.pin1
  N26: J1.B1, LM75.3
  N27: J1.B10, J39.pin2
  N28: J1.B11, J40.pin2
  N29: J1.RST, J34.pin1
  N30: J11.pin1, J3.3.3V, R26.Pin_0, J31.pin2, J32.pin1
  N31: R12.Pin_0, 7_Segment.Segment_A
  N32: R12.Pin_1, PCF8574.P0
  N33: R13.Pin_0, 7_Segment.Segment_B
  N34: R13.Pin_1, PCF8574.P1
  N35: R14.Pin_0, 7_Segment.Segment_C
  N36: R14.Pin_1, PCF8574.P2
  N37: R15.Pin_0, PCF8574.P3
  N38: R15.Pin_1, 7_Segment.Segment_D
  N39: R16.Pin_0, PCF8574.P4
  N40: R16.Pin_1, 7_Segment.Segment_E
  N41: R17.Pin_0, PCF8574.P5
  N42: R17.Pin_1, 7_Segment.Segment_F
  N43: R18.Pin_0, PCF8574.P6
  N44: R18.Pin_1, 7_Segment.Segment_G
  N45: R19.Pin_0, 7_Segment.Segment_DP
  N46: R20.Pin_0, CHG.cathode
  N47: R20.Pin_1, R21.Pin_1, U5.STAT
  N48: R21.Pin_0, DONE.anode
  N49: J6.pin1, Flash.WP, Flash.HOLD, Flash.VCC, R38.Pin_1
  N50: J7.pin1, BME280.VDDIO, BME280.VDD, C9.1, C8.1
  N51: J4.pin2, PCF8574.VCC, R30.Pin_1
  N52: J10.pin1, J8.pin2
  N53: J10.pin4, J36.pin1
  N54: J10.pin5, J9.pin2
  N55: BME280.CSB, J24.pin2
  N56: BME280.SDI, J21.pin2
  N57: BME280.SCK, J23.pin2
  N58: BME280.SDO, J22.pin2
  N59: PCF8574.P7, Joystick.SEL+
  N60: PCF8574.INT, R30.Pin_0, J25.pin2
  N61: PCF8574.SCL, J27.pin2, R28.Pin_0
  N62: PCF8574.SDA, J26.pin2, R29.Pin_0
  N63: U5.VBAT, JP1.2, D2.A, C7.+
  N64: U5.PROG, R22.Pin_1
  N65: 74VHC125MTC.3, J5.pulse
  N66: LM75.1, J40.pin1
  N67: LM75.2, J39.pin1
  N68: Buzzer.1, R27.Pin_0
  N69: Buzzer.2, Q1.collector
  N70: Flash.CS, J20.pin2, R38.Pin_0
  N71: Flash.MISO, J18.pin2
  N72: Flash.MOSI, J17.pin2
  N73: Flash.SCK, J19.pin2
  N74: J3.B12, Brake.cathode, R37.Pin_1
  N75: J3.B13, Right.cathode, J32.pin3
  N76: J3.B14, Left.cathode, J32.pin2, J33.pin2
  N77: J3.A11, J29.pin2, J30.pin1
  N78: J3.A12, J28.pin2, J30.pin2
  N79: J3.B6, J38.pin2
  N80: J3.B7, J37.pin2
  N81: J3.A0, J12.pin1
  N82: J3.B0, J34.pin2
  N83: DS1.DQ, R24.Pin_0, J35.pin2
  N84: R25.Pin_1, R26.Pin_1, J12.pin2
  N85: J14.pin2, U9.DO
  N86: J15.pin2, U9.SCK
  N87: J16.pin2, U9.CS
  N88: J13.pin2, U9.DI
  N89: R31.Pin_1, OLED.pin26
  N90: C23.1, OLED.pin6, OLED.pin9, J44.pin2, R23.Pin_1, C24.+
  N91: C22.0, OLED.pin5
  N92: C22.1, OLED.pin4
  N93: C21.0, OLED.pin3
  N94: C21.1, OLED.pin2
  N95: OLED.pin13, R23.Pin_0, J43.pin2
  N96: OLED.pin14, J40.pin3
  N97: OLED.pin15, J39.pin3
  N98: OLED.pin18, J42.pin2
  N99: OLED.pin19, J41.pin2
  N100: OLED.pin27, C25.+
  N101: OLED.pin28, C26.+
  N102: R33.Pin_0, J5.vcc
  N103: R34.Pin_0, R35.Pin_0, R36.Pin_0, J31.pin1
  N104: R34.Pin_1, Brake.anode
  N105: R35.Pin_1, Right.anode
  N106: R36.Pin_1, Left.anode
  N107: R37.Pin_0, J33.pin1

notes:
  PA0
  G
  G G3.3
  VBAT
  3.3
  RX
  TX
  5V G
  CBA_2020_10_11
  J0
  J2
  LM75

custom parts:
  7 Segment DisplayG: 7 Segment Display with common cathode.(fixed G)
  30 pin OLED: 27 pin OLED
  microSD Socket: Molex
